// Logisim project log.circ as structural Verilog
module d_latch (
  input  D,
  input  C,
  output Q
);

  wire and_1_out, and_2_out, nor_1_out, not_1_out;

  not not_1 (not_1_out, D);
  and and_1 (and_1_out, D, C);
  and and_2 (and_2_out, C, not_1_out);
  nor nor_1 (nor_1_out, and_1_out, Q);
  nor nor_2 (Q, nor_1_out, and_2_out);

  // Notes on the sheet:
  //   S
  //   R
  //   S1
  //   R1
endmodule

module d_flipflop (
  input  D,
  input  C,
  output Q
);

  wire d_latch_1_q, not_1_out;

  not not_1 (not_1_out, C);
  d_latch d_latch_1 (.D(D), .C(not_1_out), .Q(d_latch_1_q));
  d_latch d_latch_2 (.D(d_latch_1_q), .C(C), .Q(Q));
endmodule

module Register (
  input  D,
  input  C
);

  wire R0_q, R1_q, R2_q, R3_q, R4_q, R5_q, R6_q, R7_q, R8_q, R9_q, R10_q, R11_q, R12_q, R13_q, R14_q, R15_q;

  d_flipflop R1 (.D(R0_q), .C(C), .Q(R1_q));
  d_flipflop R0 (.D(D), .C(C), .Q(R0_q));
  d_flipflop R2 (.D(R1_q), .C(C), .Q(R2_q));
  d_flipflop R3 (.D(R2_q), .C(C), .Q(R3_q));
  d_flipflop R4 (.D(R3_q), .C(C), .Q(R4_q));
  d_flipflop R6 (.D(R5_q), .C(C), .Q(R6_q));
  d_flipflop R5 (.D(R4_q), .C(C), .Q(R5_q));
  d_flipflop R7 (.D(R6_q), .C(C), .Q(R7_q));
  d_flipflop R8 (.D(R7_q), .C(C), .Q(R8_q));
  d_flipflop R9 (.D(R8_q), .C(C), .Q(R9_q));
  d_flipflop R10 (.D(R9_q), .C(C), .Q(R10_q));
  d_flipflop R11 (.D(R10_q), .C(C), .Q(R11_q));
  d_flipflop R12 (.D(R11_q), .C(C), .Q(R12_q));
  d_flipflop R14 (.D(R13_q), .C(C), .Q(R14_q));
  d_flipflop R13 (.D(R12_q), .C(C), .Q(R13_q));
  d_flipflop R15 (.D(R14_q), .C(C), .Q(R15_q));
endmodule
